// Logisim project Logisim_4BitSort.circ as structural Verilog
module _1bit_swap (
  input  I1,
  input  I2,
  input  S,
  output O1,
  output O2
);

  wire and_1_out, and_2_out, and_3_out, and_4_out, not_1_out, not_2_out;

  not not_1 (not_1_out, S);
  not not_2 (not_2_out, S);
  and and_1 (and_1_out, I2, S);
  and and_2 (and_2_out, I1, not_1_out);
  and and_3 (and_3_out, I2, not_2_out);
  and and_4 (and_4_out, I1, S);
  or or_1 (O1, and_1_out, and_2_out);
  or or_2 (O2, and_3_out, and_4_out);
endmodule

module _4bit_swap (
  input  [3:0] in1,
  input  [3:0] in2,
  input  s,
  output [3:0] s1,
  output [3:0] out_5
);

  _1bit_swap u_1bit_swap_1 (.I1(in1[0]), .I2(in2[0]), .S(s), .O1(s1[0]), .O2(out_5[0]));
  _1bit_swap u_1bit_swap_2 (.I1(in1[1]), .I2(in2[1]), .S(s), .O1(s1[1]), .O2(out_5[1]));
  _1bit_swap u_1bit_swap_3 (.I1(in1[2]), .I2(in2[2]), .S(s), .O1(s1[2]), .O2(out_5[2]));
  _1bit_swap u_1bit_swap_4 (.I1(in1[3]), .I2(in2[3]), .S(s), .O1(s1[3]), .O2(out_5[3]));
endmodule

module _4bit_sort (
  input  [3:0] A,
  input  [3:0] B,
  input  [3:0] C,
  input  [3:0] D,
  output [3:0] _1,
  output [3:0] _2,
  output [3:0] _3,
  output [3:0] _4
);

  wire comparator_1_lt, comparator_2_lt, comparator_3_lt, comparator_4_lt, comparator_5_lt, comparator_6_lt;
  wire [3:0] A2, A3, B2, B3, C2, n4bit_swap_1_out_5, n4bit_swap_3_out_5, n4bit_swap_4_out_5;

  Comparator #(.width(4), .mode("unsigned")) comparator_1 (.a(A), .b(B), .lt(comparator_1_lt));  // open: gt, eq
  Comparator #(.width(4), .mode("unsigned")) comparator_2 (.a(A2), .b(B2), .lt(comparator_2_lt));  // open: gt, eq
  Comparator #(.width(4), .mode("unsigned")) comparator_3 (.a(A3), .b(B3), .lt(comparator_3_lt));  // open: gt, eq
  _4bit_swap u_4bit_swap_1 (.in1(A2), .in2(B2), .s(comparator_2_lt), .s1(A3), .out_5(n4bit_swap_1_out_5));
  _4bit_swap u_4bit_swap_2 (.in1(A3), .in2(B3), .s(comparator_3_lt), .s1(_4), .out_5(_3));
  _4bit_swap u_4bit_swap_3 (.in1(A), .in2(B), .s(comparator_1_lt), .s1(A2), .out_5(n4bit_swap_3_out_5));
  Comparator #(.width(4), .mode("unsigned")) comparator_4 (
    .a(n4bit_swap_3_out_5), .b(C), .lt(comparator_4_lt));  // open: gt, eq
  Comparator #(.width(4), .mode("unsigned")) comparator_5 (
    .a(n4bit_swap_1_out_5), .b(C2), .lt(comparator_5_lt));  // open: gt, eq
  _4bit_swap u_4bit_swap_4 (
    .in1(n4bit_swap_3_out_5), .in2(C), .s(comparator_4_lt), .s1(B2), .out_5(n4bit_swap_4_out_5));
  _4bit_swap u_4bit_swap_5 (.in1(n4bit_swap_1_out_5), .in2(C2), .s(comparator_5_lt), .s1(B3), .out_5(_2));
  Comparator #(.width(4), .mode("unsigned")) comparator_6 (
    .a(n4bit_swap_4_out_5), .b(D), .lt(comparator_6_lt));  // open: gt, eq
  _4bit_swap u_4bit_swap_6 (.in1(n4bit_swap_4_out_5), .in2(D), .s(comparator_6_lt), .s1(C2), .out_5(_1));
endmodule
