// Logisim project Logisim_fibonacci2.circ as structural Verilog: 7 circuits, main circuit main
module \矩阵乘法22  (
  input  [31:0] A,
  input  [31:0] B,
  input  [31:0] C,
  input  [31:0] D,
  input  [31:0] E,
  input  [31:0] F,
  input  [31:0] G,
  input  [31:0] H,
  output [31:0] AA,
  output [31:0] BB,
  output [31:0] CC,
  output [31:0] out_12
);

  wire [31:0] multiplier_1_out, multiplier_2_out, multiplier_3_out, multiplier_4_out, multiplier_5_out,
       multiplier_6_out, multiplier_7_out, multiplier_8_out;

  Multiplier #(.width(32)) multiplier_1 (.a(A), .b(E), .out(multiplier_1_out));  // open: cin, cout
  Multiplier #(.width(32)) multiplier_2 (.a(B), .b(G), .out(multiplier_2_out));  // open: cin, cout
  Multiplier #(.width(32)) multiplier_3 (.a(A), .b(F), .out(multiplier_3_out));  // open: cin, cout
  Multiplier #(.width(32)) multiplier_4 (.a(B), .b(H), .out(multiplier_4_out));  // open: cin, cout
  Multiplier #(.width(32)) multiplier_5 (.a(C), .b(E), .out(multiplier_5_out));  // open: cin, cout
  Multiplier #(.width(32)) multiplier_6 (.a(D), .b(G), .out(multiplier_6_out));  // open: cin, cout
  Multiplier #(.width(32)) multiplier_7 (.a(C), .b(F), .out(multiplier_7_out));  // open: cin, cout
  Multiplier #(.width(32)) multiplier_8 (.a(D), .b(H), .out(multiplier_8_out));  // open: cin, cout
  Adder #(.width(32)) adder_1 (.a(multiplier_1_out), .b(multiplier_2_out), .out(AA));  // open: cin, cout
  Adder #(.width(32)) adder_2 (.a(multiplier_3_out), .b(multiplier_4_out), .out(BB));  // open: cin, cout
  Adder #(.width(32)) adder_3 (.a(multiplier_5_out), .b(multiplier_6_out), .out(CC));  // open: cin, cout
  Adder #(.width(32)) adder_4 (.a(multiplier_7_out), .b(multiplier_8_out), .out(out_12));  // open: cin, cout

  // Other names for the same wires on the sheet: A1[31:0] = A; B1[31:0] = B; C1[31:0] = C; D1[31:0] = D; E1[31:0] = E;
  //   F1[31:0] = F; G1[31:0] = G; H1[31:0] = H
endmodule

module \矩阵乘法21  (
  input  [31:0] A,
  input  [31:0] B,
  input  [31:0] C,
  input  [31:0] D,
  input  [31:0] E,
  input  [31:0] G,
  output [31:0] AA,
  output [31:0] out_8
);

  wire [31:0] multiplier_1_out, multiplier_2_out, multiplier_3_out, multiplier_4_out;

  Multiplier #(.width(32)) multiplier_1 (.a(A), .b(E), .out(multiplier_1_out));  // open: cin, cout
  Multiplier #(.width(32)) multiplier_2 (.a(B), .b(G), .out(multiplier_2_out));  // open: cin, cout
  Multiplier #(.width(32)) multiplier_3 (.a(C), .b(E), .out(multiplier_3_out));  // open: cin, cout
  Multiplier #(.width(32)) multiplier_4 (.a(D), .b(G), .out(multiplier_4_out));  // open: cin, cout
  Adder #(.width(32)) adder_1 (.a(multiplier_1_out), .b(multiplier_2_out), .out(AA));  // open: cin, cout
  Adder #(.width(32)) adder_2 (.a(multiplier_3_out), .b(multiplier_4_out), .out(out_8));  // open: cin, cout

  // Other names for the same wires on the sheet: A1[31:0] = A; B1[31:0] = B; C1[31:0] = C; D1[31:0] = D; E1[31:0] = E;
  //   G1[31:0] = G
endmodule

module \矩阵22  (
  input  [31:0] A,
  input  [31:0] B,
  input  [31:0] C,
  input  [31:0] D,
  input  EN,
  input  CLK,
  output [31:0] AA,
  output [31:0] BB,
  output [31:0] CC,
  output [31:0] DD
);

  Register #(.width(32)) register_1 (.D(A), .en(EN), .Q(AA), .clk(CLK));  // open: clr
  Register #(.width(32)) register_2 (.D(C), .en(EN), .Q(CC), .clk(CLK));  // open: clr
  Register #(.width(32)) register_3 (.D(B), .en(EN), .Q(BB), .clk(CLK));  // open: clr
  Register #(.width(32)) register_4 (.D(D), .en(EN), .Q(DD), .clk(CLK));  // open: clr
endmodule

module \矩阵21  (
  input  [31:0] A,
  input  [31:0] B,
  input  CLK,
  output [31:0] AA,
  output [31:0] BB
);

  Register #(.width(32)) register_1 (.D(A), .Q(AA), .clk(CLK));  // open: en, clr
  Register #(.width(32)) register_2 (.D(B), .Q(BB), .clk(CLK));  // open: en, clr
endmodule

module \四复用器  (
  input  [31:0] _0,
  input  [31:0] _1,
  input  [31:0] _0_2,
  input  [31:0] _1_2,
  input  in_5,
  input  [31:0] _0_3,
  input  [31:0] _1_3,
  input  [31:0] _0_4,
  input  [31:0] _1_4,
  output [31:0] out_10,
  output [31:0] out_11,
  output [31:0] out_12,
  output [31:0] out_13
);

  Multiplexer #(.width(32)) multiplexer_1 (.in0(_0), .in1(_1), .out(out_10), .sel(in_5));  // open: en
  Multiplexer #(.width(32)) multiplexer_2 (.in0(_0_2), .in1(_1_2), .out(out_11), .sel(in_5));  // open: en
  Multiplexer #(.width(32)) multiplexer_3 (.in0(_0_3), .in1(_1_3), .out(out_12), .sel(in_5));  // open: en
  Multiplexer #(.width(32), .enable("false")) multiplexer_4 (.in0(_0_4), .in1(_1_4), .out(out_13), .sel(in_5));
endmodule

module fb (
  input  [31:0] in_1,
  input  CLK,
  output SCC,
  output [31:0] SA,
  output [31:0] SB,
  output [31:0] SC,
  output [31:0] SD
);

  wire and_2_out, cheng, comparator_1_eq, counter_1_q, cs, shuchu, undriven;
  wire [31:0] multiplexer_1_out, next, oa, ob, oc, od, out, \四复用器_1_out_10 , \四复用器_1_out_11 ,
       \四复用器_1_out_12 , \四复用器_1_out_13 , \四复用器_2_out_10 , \四复用器_2_out_11 , \四复用器_2_out_12 , \四复用器_2_out_13 ,
       \四复用器_3_out_10 , \四复用器_3_out_11 , \四复用器_3_out_12 , \四复用器_3_out_13 , \矩阵乘法22_1_aa , \矩阵乘法22_1_bb ,
       \矩阵乘法22_1_cc , \矩阵乘法22_1_out_12 , \矩阵乘法22_2_aa , \矩阵乘法22_2_bb , \矩阵乘法22_2_cc , \矩阵乘法22_2_out_12 ;

  Multiplexer #(.width(32), .enable("false")) multiplexer_1 (.in0(next), .in1(in_1), .out(multiplexer_1_out), .sel(cs));
  // Probe on undriven
  \四复用器  \u_四复用器_1  (
    ._0(\矩阵乘法22_1_aa ), ._1(32'h1), ._0_2(\矩阵乘法22_1_bb ), ._1_2(32'h1), ._0_3(\矩阵乘法22_1_cc ), ._1_3(32'h1),
    ._0_4(\矩阵乘法22_1_out_12 ), ._1_4({32{1'b0}}), .in_5(cs), .out_10(\四复用器_1_out_10 ),
    .out_11(\四复用器_1_out_11 ), .out_12(\四复用器_1_out_12 ), .out_13(\四复用器_1_out_13 ));
  Register #(.width(32)) register_1 (.D(multiplexer_1_out), .en(shuchu), .Q(out), .clk(CLK));  // open: clr
  Counter #(.width(1), .max('h1), .ongoal("stay")) counter_1 (
    .Q(counter_1_q), .clk(CLK));  // open: load, D, count, carry, clr
  \矩阵22  \u_矩阵22_1  (
    .A(\四复用器_1_out_10 ), .B(\四复用器_1_out_11 ), .C(\四复用器_1_out_12 ), .D(\四复用器_1_out_13 ), .EN(shuchu),
    .CLK(CLK), .AA(oa), .BB(ob), .CC(oc), .DD(od));
  \四复用器  \u_四复用器_2  (
    ._0(\矩阵乘法22_2_aa ), ._1(32'h1), ._0_2(\矩阵乘法22_2_bb ), ._1_2({32{1'b0}}), ._0_3(\矩阵乘法22_2_cc ),
    ._1_3({32{1'b0}}), ._0_4(\矩阵乘法22_2_out_12 ), ._1_4(32'h1), .in_5(cs), .out_10(\四复用器_2_out_10 ),
    .out_11(\四复用器_2_out_11 ), .out_12(\四复用器_2_out_12 ), .out_13(\四复用器_2_out_13 ));
  Comparator #(.width(32)) comparator_1 (.a(out), .b({32{1'b0}}), .eq(comparator_1_eq));  // open: gt, lt
  and and_1 (cheng, 1'b1, out[0]);
  Shifter #(.width(32), .shift("lr")) shifter_1 (.in(out), .\dist (5'b00001), .out(next));
  Comparator #(.width(1), .mode("unsigned")) comparator_2 (.a(counter_1_q), .b(1'b0), .eq(cs));  // open: gt, lt
  \矩阵22  \u_矩阵22_2  (
    .A(\四复用器_2_out_10 ), .B(\四复用器_2_out_11 ), .C(\四复用器_2_out_12 ), .D(\四复用器_2_out_13 ), .EN(shuchu),
    .CLK(CLK), .AA(SA), .BB(SB), .CC(SC), .DD(SD));
  \四复用器  \u_四复用器_3  (
    ._0(32'h1), ._1(oa), ._0_2({32{1'b0}}), ._1_2(ob), ._0_3({32{1'b0}}), ._1_3(oc), ._0_4(32'h1), ._1_4(od),
    .in_5(cheng), .out_10(\四复用器_3_out_10 ), .out_11(\四复用器_3_out_11 ), .out_12(\四复用器_3_out_12 ),
    .out_13(\四复用器_3_out_13 ));
  not not_1 (shuchu, and_2_out);
  and and_2 (and_2_out, comparator_1_eq, ~cs);  // AND_Gate
  \矩阵乘法22  \u_矩阵乘法22_1  (
    .A(oa), .B(ob), .C(oc), .D(od), .E(oa), .F(ob), .G(oc), .H(od), .AA(\矩阵乘法22_1_aa ), .BB(\矩阵乘法22_1_bb ),
    .CC(\矩阵乘法22_1_cc ), .out_12(\矩阵乘法22_1_out_12 ));
  \矩阵乘法22  \u_矩阵乘法22_2  (
    .A(SA), .B(SB), .C(SC), .D(SD), .E(\四复用器_3_out_10 ), .F(\四复用器_3_out_11 ), .G(\四复用器_3_out_12 ),
    .H(\四复用器_3_out_13 ), .AA(\矩阵乘法22_2_aa ), .BB(\矩阵乘法22_2_bb ), .CC(\矩阵乘法22_2_cc ),
    .out_12(\矩阵乘法22_2_out_12 ));
  not not_2 (SCC, shuchu);

  // Other names for the same wires on the sheet: In[31:0] = in_1
endmodule

module main (
  input  [31:0] IN,
  output [31:0] out_2
);

  wire clock_1_out, comparator_1_eq, comparator_1_gt, fb_1_scc, or_1_out;
  wire [31:0] demultiplexer_1_out1, fb_1_sa, fb_1_sb, fb_1_sc, fb_1_sd, multiplexer_1_out, multiplexer_2_out,
       subtractor_1_out, \四复用器_1_out_10 , \四复用器_1_out_11 , \四复用器_1_out_12 , \四复用器_1_out_13 , \矩阵乘法21_1_aa ;

  Subtractor #(.width(32)) subtractor_1 (.a(IN), .b(32'h1), .out(subtractor_1_out));  // open: bin, bout
  Demultiplexer #(.width(32), .enable("false")) demultiplexer_1 (
    .out1(demultiplexer_1_out1), .in(subtractor_1_out), .sel(comparator_1_gt));  // open: out0
  Comparator #(.width(32), .mode("unsigned")) comparator_1 (
    .a(IN), .b({32{1'b0}}), .gt(comparator_1_gt), .eq(comparator_1_eq));  // open: lt
  // Probe on demultiplexer_1_out1
  Clock clock_1 (.out(clock_1_out));
  fb fb_1 (
    .in_1(demultiplexer_1_out1), .CLK(clock_1_out), .SCC(fb_1_scc), .SA(fb_1_sa), .SB(fb_1_sb), .SC(fb_1_sc),
    .SD(fb_1_sd));
  or or_1 (or_1_out, fb_1_scc, comparator_1_eq);
  \四复用器  \u_四复用器_1  (
    ._1(fb_1_sa), ._1_2(fb_1_sb), ._1_3(fb_1_sc), ._1_4(fb_1_sd), .in_5(or_1_out), .out_10(\四复用器_1_out_10 ),
    .out_11(\四复用器_1_out_11 ), .out_12(\四复用器_1_out_12 ), .out_13(\四复用器_1_out_13 ));  // open: _0, _0_2, _0_3, _0_4
  \矩阵乘法21  \u_矩阵乘法21_1  (
    .A(\四复用器_1_out_10 ), .B(\四复用器_1_out_11 ), .C(\四复用器_1_out_12 ), .D(\四复用器_1_out_13 ), .E(32'h1),
    .G({32{1'b0}}), .AA(\矩阵乘法21_1_aa ));  // open: out_8
  Multiplexer #(.width(32), .enable("false")) multiplexer_1 (
    .in1(\矩阵乘法21_1_aa ), .out(multiplexer_1_out), .sel(fb_1_scc));  // open: in0
  Multiplexer #(.width(32), .enable("false")) multiplexer_2 (
    .in0(multiplexer_1_out), .in1({32{1'b0}}), .out(multiplexer_2_out), .sel(comparator_1_eq));
  Multiplexer #(.width(32), .enable("false")) multiplexer_3 (
    .in0({32{1'b0}}), .in1(multiplexer_2_out), .out(out_2), .sel(fb_1_scc));
endmodule
