// Logisim project Logisim_mod5.circ as structural Verilog: 3 circuits, main circuit mod5
module mod5 (
  input  in_1,
  output out_2,
  output out_3,
  output out_4,
  output out_5,
  output out_6
);

  wire clock_1_out;
  wire [1:0] register_1_q, \转移电路_1_q00 ;

  \转移电路  \u_转移电路_1  (
    .Q1(register_1_q[1]), .Q0(register_1_q[0]), .IN(in_1), .Q11(\转移电路_1_q00 [1]), .Q00(\转移电路_1_q00 [0]));
  Register #(.width(2)) register_1 (.D(\转移电路_1_q00 ), .Q(register_1_q), .clk(clock_1_out));  // open: en, clr
  Clock clock_1 (.out(clock_1_out));
  \输出电路  \u_输出电路_1  (
    .Q1(register_1_q[1]), .Q0(register_1_q[0]), .In(in_1), .S0(out_2), .S1(out_3), .S2(out_4), .S3(out_5),
    .S4(out_6));
endmodule

module \转移电路  (
  input  Q1,
  input  Q0,
  input  IN,
  output Q11,
  output Q00
);


  assign Q00 = IN;
  assign Q11 = Q0;
endmodule

module \输出电路  (
  input  Q1,
  input  Q0,
  input  In,
  output S0,
  output S1,
  output S2,
  output S3,
  output S4
);

  wire not_1_out, not_2_out, not_3_out, not_4_out;

  not not_1 (not_1_out, Q0);
  not not_2 (not_2_out, In);
  not not_3 (not_3_out, Q0);
  and and_1 (S3, Q0, In);
  not not_4 (not_4_out, In);
  and and_2 (S1, not_1_out, not_2_out);
  and and_3 (S2, not_3_out, In);
  and and_4 (S4, Q0, not_4_out);

  assign S0 = 1'b0;
endmodule
