// Logisim project P0_L0_CRC.circ as structural Verilog: 2 circuits, main circuit CRC
module CRC (
  input  [7:0] A,
  input  [3:0] B,
  output [10:0] C
);

  wire [3:1] reset, \四位模二除法器_1_r3 , \四位模二除法器_2_r3 , \四位模二除法器_3_r3 , \四位模二除法器_4_r3 , \四位模二除法器_5_r3 ,
       \四位模二除法器_6_r3 ;

  \四位模二除法器  \u_四位模二除法器_1  (.A(A[7:4]), .B(B), .R1(\四位模二除法器_1_r3 [3]), .R2(\四位模二除法器_1_r3 [2]), .R3(\四位模二除法器_1_r3 [1]));
  \四位模二除法器  \u_四位模二除法器_2  (
    .A({reset, A[0]}), .B(B), .R1(\四位模二除法器_2_r3 [3]), .R2(\四位模二除法器_2_r3 [2]), .R3(\四位模二除法器_2_r3 [1]));
  \四位模二除法器  \u_四位模二除法器_3  (
    .A({\四位模二除法器_1_r3 , A[3]}), .B(B), .R1(\四位模二除法器_3_r3 [3]), .R2(\四位模二除法器_3_r3 [2]), .R3(\四位模二除法器_3_r3 [1]));
  \四位模二除法器  \u_四位模二除法器_4  (
    .A({\四位模二除法器_2_r3 , 1'b0}), .B(B), .R1(\四位模二除法器_4_r3 [3]), .R2(\四位模二除法器_4_r3 [2]), .R3(\四位模二除法器_4_r3 [1]));
  \四位模二除法器  \u_四位模二除法器_5  (
    .A({\四位模二除法器_3_r3 , A[2]}), .B(B), .R1(\四位模二除法器_5_r3 [3]), .R2(\四位模二除法器_5_r3 [2]), .R3(\四位模二除法器_5_r3 [1]));
  \四位模二除法器  \u_四位模二除法器_6  (
    .A({\四位模二除法器_4_r3 , 1'b0}), .B(B), .R1(\四位模二除法器_6_r3 [3]), .R2(\四位模二除法器_6_r3 [2]), .R3(\四位模二除法器_6_r3 [1]));
  \四位模二除法器  \u_四位模二除法器_7  (.A({\四位模二除法器_6_r3 , 1'b0}), .B(B), .R1(C[2]), .R2(C[1]), .R3(C[0]));
  \四位模二除法器  \u_四位模二除法器_8  (.A({\四位模二除法器_5_r3 , A[1]}), .B(B), .R1(reset[3]), .R2(reset[2]), .R3(reset[1]));

  assign C[10:3] = A;

  // Other names for the same wires on the sheet: _7 = A[0]; reset[0] = A[0]; _6 = A[1]; _5 = A[2]; _4 = A[3]
endmodule

module \四位模二除法器  (
  input  [3:0] A,
  input  [3:0] B,
  output R1,
  output R2,
  output R3
);

  wire xor_1_out, xor_2_out, xor_3_out;

  xor xor_1 (xor_1_out, A[2], B[2]);
  xor xor_2 (xor_2_out, A[1], B[1]);
  xor xor_3 (xor_3_out, A[0], B[0]);
  Multiplexer #(.enable("false")) multiplexer_1 (.in0(A[2]), .in1(xor_1_out), .out(R1), .sel(A[3]));
  Multiplexer #(.enable("false")) multiplexer_2 (.in0(A[1]), .in1(xor_2_out), .out(R2), .sel(A[3]));
  Multiplexer #(.enable("false")) multiplexer_3 (.in0(A[0]), .in1(xor_3_out), .out(R3), .sel(A[3]));

  // Other names for the same wires on the sheet: _1 = A[0]; _2 = A[1]; _3 = A[2]; _4 = A[3]; B1 = B[0]; B2 = B[1];
  //   B3 = B[2]; B4 = B[3]
endmodule
