// Logisim project P0_L0_FSM.circ as structural Verilog: 3 circuits, main circuit fsm
module fsm (
  input  CLR,
  input  [1:0] in,
  output Z
);

  wire clock_1_out;
  wire [2:0] multiplexer_1_out, register_1_q, \状态转移_1_ns0 ;

  \状态转移  \u_状态转移_1  (
    .s2(register_1_q[2]), .s1(register_1_q[1]), .s0(register_1_q[0]), .in1(in[1]), .in2(in[0]),
    .ns2(\状态转移_1_ns0 [2]), .ns1(\状态转移_1_ns0 [1]), .ns0(\状态转移_1_ns0 [0]));
  Multiplexer #(.width(3), .enable("false")) multiplexer_1 (
    .in0(\状态转移_1_ns0 ), .in1(3'b000), .out(multiplexer_1_out), .sel(CLR));
  Clock clock_1 (.out(clock_1_out));
  Register #(.width(3)) register_1 (.D(multiplexer_1_out), .Q(register_1_q), .clk(clock_1_out));  // open: en, clr
  \输出  \u_输出_1  (.s2(register_1_q[2]), .s1(register_1_q[1]), .s0(register_1_q[0]), .in1(in[1]), .in0(in[0]), .Z(Z));
endmodule

module \状态转移  (
  input  s2,
  input  s1,
  input  s0,
  input  in1,
  input  in2,
  output ns2,
  output ns1,
  output ns0
);

  wire and_2_out, and_3_out, and_4_out, and_5_out, and_6_out, and_7_out, and_8_out, and_9_out, not_1_out,
       not_2_out, not_3_out, not_4_out, not_5_out, not_6_out, not_7_out, not_8_out, not_9_out, not_10_out,
       not_11_out, not_12_out, not_13_out, not_14_out, not_15_out, not_16_out, not_17_out, not_18_out,
       not_19_out, not_20_out, not_21_out, not_22_out, not_23_out, not_24_out, not_25_out;

  not not_1 (not_1_out, s2);
  not not_2 (not_2_out, in2);
  not not_3 (not_3_out, s2);
  not not_4 (not_4_out, s1);
  not not_5 (not_5_out, in1);
  not not_6 (not_6_out, s2);
  not not_7 (not_7_out, s1);
  not not_8 (not_8_out, in2);
  not not_9 (not_9_out, s2);
  not not_10 (not_10_out, s0);
  not not_11 (not_11_out, in1);
  not not_12 (not_12_out, s2);
  not not_13 (not_13_out, s0);
  not not_14 (not_14_out, in2);
  not not_15 (not_15_out, s1);
  not not_16 (not_16_out, s0);
  not not_17 (not_17_out, in1);
  not not_18 (not_18_out, s2);
  not not_19 (not_19_out, s1);
  not not_20 (not_20_out, in2);
  not not_21 (not_21_out, s2);
  not not_22 (not_22_out, s0);
  not not_23 (not_23_out, in2);
  not not_24 (not_24_out, s2);
  not not_25 (not_25_out, in1);
  and and_1 (ns2, not_1_out, s1, s0, not_2_out);
  and and_2 (and_2_out, not_3_out, not_4_out, s0, not_5_out);
  and and_3 (and_3_out, not_6_out, not_7_out, s0, not_8_out);
  and and_4 (and_4_out, not_9_out, s1, not_10_out, not_11_out);
  and and_5 (and_5_out, not_12_out, s1, not_13_out, not_14_out);
  and and_6 (and_6_out, not_15_out, not_16_out, not_17_out, in2);
  and and_7 (and_7_out, not_18_out, not_19_out, s0, not_20_out);
  and and_8 (and_8_out, not_21_out, s1, not_22_out, not_23_out);
  and and_9 (and_9_out, not_24_out, s1, s0, not_25_out, in2);
  or or_1 (ns1, and_2_out, and_3_out, and_4_out, and_5_out);
  or or_2 (ns0, and_6_out, and_7_out, and_8_out, and_9_out);
endmodule

module \输出  (
  input  s2,
  input  s1,
  input  s0,
  input  in1,
  input  in0,
  output Z
);

  wire not_1_out, not_2_out;

  not not_1 (not_1_out, s2);
  not not_2 (not_2_out, in0);
  and and_1 (Z, not_1_out, s1, s0, not_2_out);
endmodule
