// Logisim project P0_L0_GRF.circ as structural Verilog: 2 circuits, main circuit grf
module grf (
  input  CLK,
  input  Reset,
  input  WE,
  input  [4:0] A1,
  input  [4:0] A2,
  input  [4:0] A3,
  input  [31:0] WD,
  output [31:0] RD1,
  output [31:0] RD2
);

  wire [31:0] data1, data2, data3, data4, data5, data6, data7, data8, data9, data10, data11, data12, data13,
       data14, data15, data16, data17, data18, data19, data20, data21, data22, data23, data24, data25,
       data26, data27, data28, data29, data30, data31, out0, out1, out2, out3, out4, out5, out6, out7, out8,
       out9, out10, out11, out12, out13, out14, out15, out16, out17, out18, out19, out20, out21, out22,
       out23, out24, out25, out26, out27, out28, out29, out30, out31;

  Demultiplexer #(.select(5), .width(32), .tristate("true")) demultiplexer_1 (
    .out1(data1), .out2(data2), .out3(data3), .out4(data4), .out5(data5), .out6(data6), .out7(data7),
    .out8(data8), .out9(data9), .out10(data10), .out11(data11), .out12(data12), .out13(data13),
    .out14(data14), .out15(data15), .out16(data16), .out17(data17), .out18(data18), .out19(data19),
    .out20(data20), .out21(data21), .out22(data22), .out23(data23), .out24(data24), .out25(data25),
    .out26(data26), .out27(data27), .out28(data28), .out29(data29), .out30(data30), .out31(data31), .in(WD),
    .sel(A3), .en(WE));  // open: out0
  Register #(.width(32)) _0 (.Q(out0), .clr(1'b1));  // open: D, en, clk
  Register #(.width(32)) _8 (.D(data8), .Q(out8), .clk(CLK), .clr(Reset));  // open: en
  Register #(.width(32)) _16 (.D(data16), .Q(out16), .clk(CLK), .clr(Reset));  // open: en
  Register #(.width(32)) _24 (.D(data24), .Q(out24), .clk(CLK), .clr(Reset));  // open: en
  Register #(.width(32)) _1 (.D(data1), .Q(out1), .clk(CLK), .clr(Reset));  // open: en
  Register #(.width(32)) _9 (.D(data9), .Q(out9), .clk(CLK), .clr(Reset));  // open: en
  Register #(.width(32)) _17 (.D(data17), .Q(out17), .clk(CLK), .clr(Reset));  // open: en
  Register #(.width(32)) _25 (.D(data25), .Q(out25), .clk(CLK), .clr(Reset));  // open: en
  Register #(.width(32)) _2 (.D(data2), .Q(out2), .clk(CLK), .clr(Reset));  // open: en
  Register #(.width(32)) _10 (.D(data10), .Q(out10), .clk(CLK), .clr(Reset));  // open: en
  Register #(.width(32)) _18 (.D(data18), .Q(out18), .clk(CLK), .clr(Reset));  // open: en
  Register #(.width(32)) _26 (.D(data26), .Q(out26), .clk(CLK), .clr(Reset));  // open: en
  Register #(.width(32)) _3 (.D(data3), .Q(out3), .clk(CLK), .clr(Reset));  // open: en
  Register #(.width(32)) _11 (.D(data11), .Q(out11), .clk(CLK), .clr(Reset));  // open: en
  Register #(.width(32)) _19 (.D(data19), .Q(out19), .clk(CLK), .clr(Reset));  // open: en
  Register #(.width(32)) _27 (.D(data27), .Q(out27), .clk(CLK), .clr(Reset));  // open: en
  Register #(.width(32)) _4 (.D(data4), .Q(out4), .clk(CLK), .clr(Reset));  // open: en
  Register #(.width(32)) _12 (.D(data12), .Q(out12), .clk(CLK), .clr(Reset));  // open: en
  Register #(.width(32)) _20 (.D(data20), .Q(out20), .clk(CLK), .clr(Reset));  // open: en
  Register #(.width(32)) _28 (.D(data28), .Q(out28), .clk(CLK), .clr(Reset));  // open: en
  Register #(.width(32)) _5 (.D(data5), .Q(out5), .clk(CLK), .clr(Reset));  // open: en
  Register #(.width(32)) _21 (.D(data21), .Q(out21), .clk(CLK), .clr(Reset));  // open: en
  Register #(.width(32)) _29 (.D(data29), .Q(out29), .clk(CLK), .clr(Reset));  // open: en
  Register #(.width(32)) _13 (.D(data13), .Q(out13), .clk(CLK), .clr(Reset));  // open: en
  Register #(.width(32)) _6 (.D(data6), .Q(out6), .clk(CLK), .clr(Reset));  // open: en
  Register #(.width(32)) _14 (.D(data14), .Q(out14), .clk(CLK), .clr(Reset));  // open: en
  Register #(.width(32)) _22 (.D(data22), .Q(out22), .clk(CLK), .clr(Reset));  // open: en
  Register #(.width(32)) _30 (.D(data30), .Q(out30), .clk(CLK), .clr(Reset));  // open: en
  Register #(.width(32)) _31 (.D(data31), .Q(out31), .clk(CLK), .clr(Reset));  // open: en
  Register #(.width(32)) _7 (.D(data7), .Q(out7), .clk(CLK), .clr(Reset));  // open: en
  Register #(.width(32)) _15 (.D(data15), .Q(out15), .clk(CLK), .clr(Reset));  // open: en
  Register #(.width(32)) _23 (.D(data23), .Q(out23), .clk(CLK), .clr(Reset));  // open: en
  Multiplexer #(.select(5), .width(32), .disabled(0)) multiplexer_1 (
    .in0(out0), .in1(out1), .in2(out2), .in3(out3), .in4(out4), .in5(out5), .in6(out6), .in7(out7),
    .in8(out8), .in9(out9), .in10(out10), .in11(out11), .in12(out12), .in13(out13), .in14(out14),
    .in15(out15), .in16(out16), .in17(out17), .in18(out18), .in19(out19), .in20(out20), .in21(out21),
    .in22(out22), .in23(out23), .in24(out24), .in25(out25), .in26(out26), .in27(out27), .in28(out28),
    .in29(out29), .in30(out30), .in31(out31), .out(RD1), .sel(A1));  // open: en
  Multiplexer #(.select(5), .width(32), .disabled(0)) multiplexer_2 (
    .in0(out0), .in1(out1), .in2(out2), .in3(out3), .in4(out4), .in5(out5), .in6(out6), .in7(out7),
    .in8(out8), .in9(out9), .in10(out10), .in11(out11), .in12(out12), .in13(out13), .in14(out14),
    .in15(out15), .in16(out16), .in17(out17), .in18(out18), .in19(out19), .in20(out20), .in21(out21),
    .in22(out22), .in23(out23), .in24(out24), .in25(out25), .in26(out26), .in27(out27), .in28(out28),
    .in29(out29), .in30(out30), .in31(out31), .out(RD2), .sel(A2));  // open: en
endmodule

module _15 (
);

  grf grf_1 ();  // open: CLK, Reset, WE, A1, A2, A3, WD, RD1, RD2
endmodule
