// Logisim project P0_L1_ftoi.circ as structural Verilog: 2 circuits, main circuit ftoi
module ftoi (
  input  [15:0] float,
  output [31:0] \int 
);

  wire comparator_1_eq, comparator_2_eq, less0, no, o0, or_2_out;
  wire [4:0] subtractor_2_out, weiyi, yiwei;
  wire [31:0] buma_1_out_2, buma_2_out_2, Fnial, multiplexer_1_out, negator_1_out, shifter_1_out,
       shifter_2_out, zhengshu;

  Comparator #(.width(5), .mode("unsigned")) comparator_1 (
    .a(float[14:10]), .b({5{1'b1}}), .eq(comparator_1_eq));  // open: gt, lt
  Comparator #(.width(5), .mode("unsigned")) comparator_2 (
    .a(float[14:10]), .b({5{1'b0}}), .eq(comparator_2_eq));  // open: gt, lt
  // Probe on weiyi
  Subtractor #(.width(5)) subtractor_1 (.a(float[14:10]), .b(5'b01111), .out(weiyi));  // open: bin, bout
  buma buma_1 (.frac(float[9:0]), .out_2(buma_1_out_2));
  buma buma_2 (.frac(float[9:0]), .out_2(buma_2_out_2));
  Comparator #(.width(5)) comparator_3 (.a(weiyi), .b({5{1'b0}}), .lt(less0));  // open: gt, eq
  Subtractor #(.width(5)) subtractor_2 (.a(weiyi), .b(5'b01010), .out(subtractor_2_out));  // open: bin, bout
  // Probe on subtractor_2_out
  or or_1 (o0, comparator_1_eq, comparator_2_eq);
  Shifter #(.width(32)) shifter_1 (.in(zhengshu), .\dist (subtractor_2_out), .out(shifter_1_out));
  // Probe on yiwei
  Subtractor #(.width(5)) subtractor_3 (.a(5'b01010), .b(weiyi), .out(yiwei));  // open: bin, bout
  or or_2 (or_2_out, o0, less0);
  Comparator #(.width(5)) comparator_4 (.a(yiwei), .b({5{1'b0}}), .lt(no));  // open: gt, eq
  Shifter #(.width(32), .shift("ar")) shifter_2 (.in(buma_1_out_2), .\dist (yiwei), .out(shifter_2_out));
  // Probe on buma_2_out_2
  Multiplexer #(.width(32), .enable("false")) multiplexer_1 (
    .in0(zhengshu), .in1(shifter_1_out), .out(multiplexer_1_out), .sel(no));
  Multiplexer #(.width(32), .enable("false")) multiplexer_2 (
    .in0(shifter_2_out), .in1(buma_2_out_2), .out(zhengshu), .sel(no));
  Multiplexer #(.width(32), .enable("false")) multiplexer_3 (
    .in0(Fnial), .in1({32{1'b0}}), .out(\int ), .sel(or_2_out));
  Negator #(.width(32)) negator_1 (.in(multiplexer_1_out), .out(negator_1_out));
  Multiplexer #(.width(32), .enable("false")) multiplexer_4 (
    .in0(multiplexer_1_out), .in1(negator_1_out), .out(Fnial), .sel(float[15]));

  // Other names for the same wires on the sheet: frac[9:0] = float[9:0]; e[4:0] = float[14:10]; sign = float[15]
endmodule

module buma (
  input  [9:0] frac,
  output [31:0] out_2
);

  assign out_2 = {{21{1'b0}}, {1'b1, frac}};  // Bit_Extender bit_extender_1

  // Other names for the same wires on the sheet: _1[9:0] = frac
endmodule
