// Logisim project fb.circ as structural Verilog
module main (
  input  [2:0] N,
  output [3:0] out_2
);

  wire clock_1_out, comparator_1_eq, comparator_2_eq, multiplexer_2_out, not_1_out, or_1_out, register_3_q;
  wire [2:0] counter_1_q;
  wire [3:0] multiplexer_1_out, register_1_q, register_2_q, \计算_1_out_3 ;

  not not_1 (not_1_out, or_1_out);
  Register #(.width(4)) register_1 (
    .D(multiplexer_1_out), .en(not_1_out), .Q(register_1_q), .clk(clock_1_out));  // open: clr
  Register #(.width(4)) register_2 (.D(register_1_q), .Q(register_2_q), .clk(clock_1_out));  // open: en, clr
  Counter #(.width(3), .max('h7)) counter_1 (.Q(counter_1_q), .clk(clock_1_out));  // open: load, D, count, carry, clr
  Clock clock_1 (.out(clock_1_out));
  \计算  \u_计算_1  (.in_1(register_1_q), .in_2(register_2_q), .out_3(\计算_1_out_3 ));
  Multiplexer #(.width(4), .enable("false")) multiplexer_1 (
    .in0(\计算_1_out_3 ), .in1(4'b0001), .out(multiplexer_1_out), .sel(comparator_1_eq));
  Comparator #(.width(4)) comparator_1 (.a(\计算_1_out_3 ), .b(4'b0000), .eq(comparator_1_eq));  // open: gt, lt
  Comparator #(.width(3)) comparator_2 (.a(counter_1_q), .b(N), .eq(comparator_2_eq));  // open: gt, lt
  Register #(.width(1)) register_3 (.D(multiplexer_2_out), .Q(register_3_q), .clk(clock_1_out));  // open: en, clr
  Multiplexer multiplexer_2 (.in1(1'b1), .out(multiplexer_2_out), .sel(comparator_2_eq));  // open: in0, en
  or or_1 (or_1_out, register_3_q, comparator_2_eq);
  Multiplexer #(.width(4), .enable("false")) multiplexer_3 (
    .in0(4'b0000), .in1(register_1_q), .out(out_2), .sel(or_1_out));
endmodule

module \计算  (
  input  [3:0] in_1,
  input  [3:0] in_2,
  output [3:0] out_3
);

  Adder #(.width(4)) adder_1 (.a(in_1), .b(in_2), .out(out_3));  // open: cin, cout
endmodule
