// Logisim project h1.circ as structural Verilog: 2 circuits, main circuit main
module main (
  input  l1,
  input  l2,
  input  l3,
  output o1,
  output o2,
  output o3
);
endmodule

module h1 (
  input  l1,
  input  l2,
  input  l3,
  output o1,
  output o2,
  output o3
);

  wire and_1_out, and_2_out, and_3_out, not_1_out, not_2_out, not_3_out, not_4_out;

  not not_1 (not_1_out, l1);
  not not_2 (not_2_out, l1);
  not not_3 (not_3_out, l1);
  not not_4 (not_4_out, l3);
  and and_1 (and_1_out, not_1_out, l3);
  and and_2 (and_2_out, not_2_out, l2);
  and and_3 (and_3_out, not_3_out, not_4_out);
  or or_1 (o1, and_1_out, and_2_out);
  or or_2 (o2, and_3_out, l2);

  assign o3 = l3;
endmodule
