// Logisim project mod5.circ as structural Verilog: 3 circuits, main circuit mod5
module mod5 (
  input  in_1,
  output s0,
  output s1,
  output s2,
  output s3,
  output s4
);

  wire clock_1_out, register_1_q, \转移_1_s00 ;

  \转移  \u_转移_1  (.S0(register_1_q), .IN(in_1), .S00(\转移_1_s00 ));
  Clock clock_1 (.out(clock_1_out));
  Register #(.width(1)) register_1 (.D(\转移_1_s00 ), .Q(register_1_q), .clk(clock_1_out));  // open: en, clr
  \输出  \u_输出_1  (.cs(register_1_q), .in(in_1), .S0(s0), .S1(s1), .S2(s2), .S3(s3), .S4(s4));
endmodule

module \转移  (
  input  S0,
  input  IN,
  output S00
);


  assign S00 = IN;
endmodule

module \输出  (
  input  cs,
  input  in,
  output S0,
  output S1,
  output S2,
  output S3,
  output S4
);

  wire not_1_out, not_2_out, not_3_out, not_4_out;

  not not_1 (not_1_out, cs);
  not not_2 (not_2_out, in);
  not not_3 (not_3_out, cs);
  and and_1 (S3, cs, in);
  not not_4 (not_4_out, in);
  and and_2 (S1, not_1_out, not_2_out);
  and and_3 (S2, not_3_out, in);
  and and_4 (S4, cs, not_4_out);

  assign S0 = 1'b0;
endmodule
