// Logisim project 八位移位器.circ as structural Verilog
module \_8位移位器  (
  input  [2:0] in_1,
  input  in_2,
  input  in_3,
  input  in_4,
  input  in_5,
  input  in_6,
  input  in_7,
  input  in_8,
  input  in_9,
  output out_10,
  output out_11,
  output out_12,
  output out_13,
  output out_14,
  output out_15,
  output out_16,
  output out_17
);

  Multiplexer #(.select(3), .enable("false")) multiplexer_1 (
    .in0(in_2), .in1(in_3), .in2(in_4), .in3(in_5), .in4(in_6), .in5(in_7), .in6(in_8), .in7(in_9),
    .out(out_10), .sel(in_1));
  Multiplexer #(.select(3), .enable("false")) multiplexer_2 (
    .in0(in_3), .in1(in_4), .in2(in_5), .in3(in_6), .in4(in_7), .in5(in_8), .in6(in_9), .in7(1'b0),
    .out(out_11), .sel(in_1));
  Multiplexer #(.select(3), .enable("false")) multiplexer_3 (
    .in0(in_4), .in1(in_5), .in2(in_6), .in3(in_7), .in4(in_8), .in5(in_9), .in6(1'b0), .in7(1'b0),
    .out(out_12), .sel(in_1));
  Multiplexer #(.select(3), .enable("false")) multiplexer_4 (
    .in0(in_5), .in1(in_6), .in2(in_7), .in3(in_8), .in4(in_9), .in5(1'b0), .in6(1'b0), .in7(1'b0),
    .out(out_13), .sel(in_1));
  Multiplexer #(.select(3), .enable("false")) multiplexer_5 (
    .in0(in_6), .in1(in_7), .in2(in_8), .in3(in_9), .in4(1'b0), .in5(1'b0), .in6(1'b0), .in7(1'b0),
    .out(out_14), .sel(in_1));
  Multiplexer #(.select(3), .enable("false")) multiplexer_6 (
    .in0(in_7), .in1(in_8), .in2(in_9), .in3(1'b0), .in4(1'b0), .in5(1'b0), .in7(1'b0), .out(out_15),
    .sel(in_1));  // open: in6
  Multiplexer #(.select(3), .enable("false")) multiplexer_7 (
    .in0(in_8), .in1(in_9), .in2(1'b0), .in3(1'b0), .in4(1'b0), .in5(1'b0), .in6(1'b0), .in7(1'b0),
    .out(out_16), .sel(in_1));
  Multiplexer #(.select(3), .enable("false")) multiplexer_8 (
    .in0(in_9), .in1(1'b0), .in2(1'b0), .in3(1'b0), .in4(1'b0), .in6(1'b0), .in7(1'b0), .out(out_17),
    .sel(in_1));  // open: in5
endmodule
