// Logisim project 售货机.circ as structural Verilog: 3 circuits, main circuit main
module main (
  input  [1:0] in,
  output out_2,
  output [2:0] out_3
);

  wire clock_1_out;
  wire [3:0] register_1_q, \状态转移哦_1_ns0 ;

  \状态转移哦  \u_状态转移哦_1  (
    .s3(register_1_q[3]), .s2(register_1_q[2]), .s1(register_1_q[1]), .s0(register_1_q[0]), .in1(in[1]),
    .in0(in[0]), .ns3(\状态转移哦_1_ns0 [3]), .ns2(\状态转移哦_1_ns0 [2]), .ns1(\状态转移哦_1_ns0 [1]),
    .ns0(\状态转移哦_1_ns0 [0]));
  Clock clock_1 (.out(clock_1_out));
  Register #(.width(4)) register_1 (.D(\状态转移哦_1_ns0 ), .Q(register_1_q), .clk(clock_1_out));  // open: en, clr
  \输出  \u_输出_1  (
    .s3(register_1_q[3]), .s2(register_1_q[2]), .s1(register_1_q[1]), .s0(register_1_q[0]), .dispense(out_2),
    .res2(out_3[2]), .res1(out_3[1]), .res0(out_3[0]));
endmodule

module \状态转移哦  (
  input  s3,
  input  s2,
  input  s1,
  input  s0,
  input  in1,
  input  in0,
  output ns3,
  output ns2,
  output ns1,
  output ns0
);

  wire and_1_out, and_2_out, and_3_out, and_4_out, and_5_out, and_6_out, and_7_out, and_8_out, and_9_out,
       and_10_out, and_11_out, and_12_out, and_13_out, and_14_out, and_15_out, and_16_out, not_1_out,
       not_2_out, not_3_out, not_4_out, not_5_out, not_6_out, not_7_out, not_8_out, not_9_out, not_10_out,
       not_11_out, not_12_out, not_13_out, not_14_out, not_15_out, not_16_out, not_17_out, not_18_out,
       not_19_out, not_20_out, not_21_out, not_22_out, not_23_out, not_24_out, not_25_out, not_26_out,
       not_27_out, not_28_out, not_29_out, not_30_out, not_31_out, not_32_out, not_33_out, not_34_out,
       not_35_out, not_36_out, not_37_out, not_38_out, not_39_out, not_40_out, not_41_out, not_42_out,
       not_43_out, not_44_out, not_45_out, not_46_out, not_47_out, not_48_out, not_49_out, not_50_out,
       not_51_out, not_52_out;

  not not_1 (not_1_out, s3);
  not not_2 (not_2_out, s2);
  not not_3 (not_3_out, s3);
  not not_4 (not_4_out, s1);
  not not_5 (not_5_out, s0);
  not not_6 (not_6_out, s3);
  not not_7 (not_7_out, s2);
  not not_8 (not_8_out, s1);
  not not_9 (not_9_out, s3);
  not not_10 (not_10_out, s2);
  not not_11 (not_11_out, s0);
  not not_12 (not_12_out, s3);
  not not_13 (not_13_out, s2);
  not not_14 (not_14_out, in0);
  not not_15 (not_15_out, s3);
  not not_16 (not_16_out, s2);
  not not_17 (not_17_out, in1);
  not not_18 (not_18_out, s3);
  not not_19 (not_19_out, s1);
  not not_20 (not_20_out, s0);
  not not_21 (not_21_out, in1);
  not not_22 (not_22_out, s3);
  not not_23 (not_23_out, s1);
  not not_24 (not_24_out, s0);
  not not_25 (not_25_out, in0);
  not not_26 (not_26_out, s3);
  not not_27 (not_27_out, s2);
  not not_28 (not_28_out, s1);
  not not_29 (not_29_out, in0);
  not not_30 (not_30_out, s3);
  not not_31 (not_31_out, s1);
  not not_32 (not_32_out, s0);
  not not_33 (not_33_out, in0);
  not not_34 (not_34_out, s3);
  not not_35 (not_35_out, s2);
  not not_36 (not_36_out, s1);
  not not_37 (not_37_out, s3);
  not not_38 (not_38_out, s2);
  not not_39 (not_39_out, in1);
  not not_40 (not_40_out, in0);
  not not_41 (not_41_out, s3);
  not not_42 (not_42_out, s2);
  not not_43 (not_43_out, s0);
  not not_44 (not_44_out, s3);
  not not_45 (not_45_out, s2);
  not not_46 (not_46_out, s0);
  not not_47 (not_47_out, s3);
  not not_48 (not_48_out, s1);
  not not_49 (not_49_out, s0);
  not not_50 (not_50_out, s3);
  not not_51 (not_51_out, s2);
  not not_52 (not_52_out, in0);
  and and_1 (and_1_out, not_1_out, not_2_out, s1, s0, in1, in0);
  and and_2 (and_2_out, not_3_out, s2, not_4_out, not_5_out, in1, in0);
  and and_3 (and_3_out, not_6_out, not_7_out, not_8_out, in1, in0);
  and and_4 (and_4_out, not_9_out, not_10_out, s1, not_11_out, in1);
  and and_5 (and_5_out, not_12_out, not_13_out, s1, in1, not_14_out);
  and and_6 (and_6_out, not_15_out, not_16_out, s1, s0, not_17_out, in0);
  and and_7 (and_7_out, not_18_out, s2, not_19_out, not_20_out, not_21_out);
  and and_8 (and_8_out, not_22_out, s2, not_23_out, not_24_out, not_25_out);
  and and_9 (and_9_out, not_26_out, not_27_out, not_28_out, in1, not_29_out);
  and and_10 (and_10_out, not_30_out, not_31_out, not_32_out, in1, not_33_out);
  and and_11 (and_11_out, not_34_out, not_35_out, not_36_out, s0, in0);
  and and_12 (and_12_out, not_37_out, not_38_out, s1, not_39_out, not_40_out);
  and and_13 (and_13_out, not_41_out, not_42_out, s1, not_43_out, in0);
  and and_14 (and_14_out, not_44_out, not_45_out, not_46_out, in0);
  and and_15 (and_15_out, not_47_out, not_48_out, not_49_out, in0);
  and and_16 (and_16_out, not_50_out, not_51_out, s0, not_52_out);
  or or_1 (ns3, and_1_out, and_2_out);
  or or_2 (ns2, and_3_out, and_4_out, and_5_out, and_6_out, and_7_out, and_8_out);
  or or_3 (ns1, and_9_out, and_10_out, and_11_out, and_12_out, and_13_out);
  or or_4 (ns0, and_14_out, and_15_out, and_16_out);
endmodule

module \输出  (
  input  s3,
  input  s2,
  input  s1,
  input  s0,
  output dispense,
  output res2,
  output res1,
  output res0
);

  wire and_1_out, and_2_out, and_4_out, and_5_out, and_6_out, and_7_out, not_1_out, not_2_out, not_3_out;

  and and_1 (and_1_out, s2, s0);
  and and_2 (and_2_out, s2, s1);
  and and_3 (res2, s3, s0);
  and and_4 (and_4_out, s2, s1, s0);
  and and_5 (and_5_out, s3, not_1_out);
  not not_1 (not_1_out, s0);
  and and_6 (and_6_out, s2, s1, not_2_out);
  not not_2 (not_2_out, s0);
  and and_7 (and_7_out, s3, not_3_out);
  not not_3 (not_3_out, s0);
  or or_1 (dispense, and_1_out, and_2_out, s3);
  or or_2 (res1, and_4_out, and_5_out);
  or or_3 (res0, and_6_out, and_7_out);
endmodule
