// Logisim project 斐波那契数列.circ as structural Verilog: 1 circuit, main circuit main
module main (
  input  [2:0] N,
  output [3:0] Nth
);

  wire CLK, comparator_1_eq, comparator_1_lt, counter_2_q, Freeze, Init, or_1_out;
  wire [2:0] counter_1_q;
  wire [3:0] adder_1_out, F0, F1, multiplexer_1_out, multiplexer_2_out;

  Clock clock_1 (.out(CLK));
  Counter #(.width(3), .max('h7), .ongoal("stay")) counter_1 (
    .Q(counter_1_q), .clk(CLK));  // open: load, D, count, carry, clr
  Adder #(.width(4)) adder_1 (.a(F0), .b(F1), .out(adder_1_out));  // open: cin, cout
  Multiplexer #(.width(4), .enable("false")) multiplexer_1 (
    .in0(adder_1_out), .in1(4'b0001), .out(multiplexer_1_out), .sel(Init));
  Multiplexer #(.width(4), .enable("false")) multiplexer_2 (
    .in0(F1), .in1(4'b0000), .out(multiplexer_2_out), .sel(Init));
  Comparator #(.width(3), .mode("unsigned")) comparator_1 (
    .a(N), .b(counter_1_q), .eq(comparator_1_eq), .lt(comparator_1_lt));  // open: gt
  not not_1 (Freeze, or_1_out);
  or or_1 (or_1_out, comparator_1_eq, comparator_1_lt);
  Register #(.width(4)) register_1 (.D(multiplexer_1_out), .en(Freeze), .Q(F1), .clk(CLK));  // open: clr
  Register #(.width(4)) register_2 (.D(multiplexer_2_out), .en(Freeze), .Q(F0), .clk(CLK));  // open: clr
  Counter #(.width(1), .max('h1), .ongoal("stay")) counter_2 (
    .Q(counter_2_q), .clk(CLK));  // open: load, D, count, carry, clr
  Multiplexer #(.width(4), .enable("false")) multiplexer_3 (.in0(F1), .in1(4'b0000), .out(Nth), .sel(Freeze));
  not not_2 (Init, counter_2_q);
endmodule
