// Logisim project 测试.circ as structural Verilog
module \一位全加器  (
  input  A,
  input  B,
  input  Cin,
  input  [5:0] in_4,
  output S,
  output Cout
);

  wire and_1_out, and_2_out, xor_1_out, xor_2_out;
  wire [2:0] xnor_1_out;

  Bit_Extender bit_extender_1 ();  // open: in, out
  xor xor_1 (xor_1_out, A, B);
  and and_1 (and_1_out, A, B);
  and and_2 (and_2_out, Cin, xor_2_out);
  xor xor_2 (xor_2_out, A, B);
  Bit_Extender #(.\type ("input")) bit_extender_2 ();  // open: in, out, extend
  BitSelector bitselector_1 ();  // open: in, out, sel
  xor xor_3 (S, xor_1_out, Cin);
  or or_1 (Cout, and_1_out, and_2_out);
  // Probe on xnor_1_out
  assign xnor_1_out = ~(in_4[2:0] ^ in_4[5:3]);  // XNOR_Gate xnor_1, 3 bits wide
endmodule
