// Logisim project 第 ii 个周期，寄存器的值被更新为 2^i2  i.circ as structural Verilog: 1 circuit, main circuit main
module main (
  output [31:0] out_1
);

  wire CLK, Init;
  wire [31:0] multiplexer_1_out, shifter_1_out;

  Clock clock_1 (.out(CLK));
  Shifter #(.width(32)) shifter_1 (.in(out_1), .\dist (5'b00001), .out(shifter_1_out));
  Multiplexer #(.width(32), .enable("false")) multiplexer_1 (
    .in0(32'h2), .in1(shifter_1_out), .out(multiplexer_1_out), .sel(Init));
  Counter #(.width(1), .max('h1), .ongoal("stay")) counter_1 (.Q(Init), .clk(CLK));  // open: load, D, count, carry, clr
  Register #(.width(32)) register_1 (.D(multiplexer_1_out), .Q(out_1), .clk(CLK));  // open: en, clr
endmodule
