// Logisim project CPU3.circ as structural Verilog: 6 circuits, main circuit main
module main (
  input  in_1,
  output [31:0] Instr,
  output RegWrite,
  output [4:0] RegAddr,
  output [31:0] RegData,
  output MemWrite,
  output [4:0] MemAddr,
  output [31:0] MemData
);

  wire clk;
  wire [1:0] alua, DMDATAMUX, EXTOP, SBSELC;
  wire [2:0] alub, NPCOP, RFA3MUX, RFWDMUX;
  wire [3:0] control_1_aluop;
  wire [4:0] alu_1_zero, NPC_2_rd, NPC_2_rs, NPC_2_rt, NPC_2_shamt;
  wire [5:0] NPC_2_func, NPC_2_opcode;
  wire [15:0] NPC_2_imm0_16;
  wire [25:0] NPC_2_imm26;
  wire [31:0] bit_extender_1_out, bit_extender_2_out, bit_extender_3_out, DMDATA, grf_1_rd1, grf_1_rd2,
       multiplexer_3_out, multiplexer_4_out, multiplexer_5_out, multiplexer_7_out, npc_1_npc, PC_4, PC_q;
  wire [31:7] alu_1_aluout;

  Clock clock_1 (.out(clk));
  Register #(.width(32)) PC (.D(npc_1_npc), .Q(PC_q), .clk(clk), .clr(in_1));  // open: en
  NPC npc_1 (
    .NPCOP(NPCOP), .Zero(alu_1_zero), .PC(PC_q), .IMM26(NPC_2_imm26), .IMM16(NPC_2_imm0_16),
    .imm32({alu_1_aluout, MemAddr, SBSELC}), .PC_4(PC_4), .NPC(npc_1_npc));
  ROM #(.addrWidth(24), .dataWidth(32)) rom_1 (.addr(PC_q[25:2]), .data(Instr));  // open: sel
  \分线器  NPC_2 (
    .in_1(Instr), .OPcode(NPC_2_opcode), .rs(NPC_2_rs), .rt(NPC_2_rt), .rd(NPC_2_rd), .shamt(NPC_2_shamt),
    .func(NPC_2_func), .imm0_16(NPC_2_imm0_16), .imm26(NPC_2_imm26));
  Control control_1 (
    .opcode(NPC_2_opcode), .func(NPC_2_func), .npcop(NPCOP), .rfwe(RegWrite), .ALUOP(control_1_aluop),
    .EXTOP(EXTOP), .DMWE(MemWrite), .RFA3MUX(RFA3MUX), .RFWDMUX(RFWDMUX), .AUBMUX(alub), .ALUAMUX(alua),
    .DMDATAMUX(DMDATAMUX));
  assign bit_extender_1_out = {{16{1'b0}}, NPC_2_imm0_16};  // Bit_Extender bit_extender_1
  assign bit_extender_2_out = {{27{1'b0}}, NPC_2_shamt};  // Bit_Extender bit_extender_2
  Multiplexer #(.select(3), .width(5), .enable("false")) multiplexer_1 (
    .in0(NPC_2_rd), .in1(NPC_2_rt), .in2({5{1'b1}}), .out(RegAddr), .sel(RFA3MUX));  // open: in3, in4, in5, in6, in7
  Multiplexer #(.select(3), .width(32), .enable("false")) multiplexer_2 (
    .in0({alu_1_aluout, MemAddr, SBSELC}), .in1(DMDATA), .in2(PC_4), .out(RegData), .sel(RFWDMUX));  // open: in3, in4, in5, in6, in7
  assign bit_extender_3_out = {{16{NPC_2_imm0_16[15]}}, NPC_2_imm0_16};  // Bit_Extender bit_extender_3
  Multiplexer #(.select(2), .width(32), .enable("false")) multiplexer_3 (
    .in0(bit_extender_3_out), .in1(bit_extender_1_out), .in2(bit_extender_2_out), .out(multiplexer_3_out),
    .sel(EXTOP));  // open: in3
  GRF grf_1 (
    .CLK(clk), .Reset(in_1), .WE(RegWrite), .A1(NPC_2_rs), .A2(NPC_2_rt), .A3(RegAddr), .WD(RegData),
    .RD1(grf_1_rd1), .RD2(grf_1_rd2));
  Multiplexer #(.select(2), .width(32), .enable("false")) multiplexer_4 (
    .in0(grf_1_rd1), .in1(grf_1_rd2), .out(multiplexer_4_out), .sel(alua));  // open: in2, in3
  Multiplexer #(.select(3), .width(32), .enable("false")) multiplexer_5 (
    .in0(grf_1_rd2), .in1(multiplexer_3_out), .out(multiplexer_5_out), .sel(alub));  // open: in2, in3, in4, in5, in6, in7
  ALU alu_1 (
    .ALUOP(control_1_aluop), .A(multiplexer_4_out), .B(multiplexer_5_out), .Zero(alu_1_zero),
    .ALUOUT({alu_1_aluout, MemAddr, SBSELC}));
  // Probe on SBSELC
  Multiplexer #(.select(2), .width(32), .enable("false")) multiplexer_6 (
    .in0(grf_1_rd2), .in1(multiplexer_7_out), .out(MemData), .sel(DMDATAMUX));  // open: in2, in3
  RAM #(.addrWidth(24), .dataWidth(32), .bus("separate")) ram_1 (
    .addr({alu_1_aluout[25:7], MemAddr}), .din(MemData), .data(DMDATA), .str(MemWrite), .clk(clk), .clr(in_1));  // open: sel, ld
  Multiplexer #(.select(2), .width(32), .enable("false")) multiplexer_7 (
    .in0({DMDATA[31:8], grf_1_rd2[7:0]}), .in1({DMDATA[31:16], grf_1_rd2[7:0], DMDATA[7:0]}),
    .in2({DMDATA[31:24], grf_1_rd2[7:0], DMDATA[15:0]}), .in3({grf_1_rd2[7:0], DMDATA[23:0]}),
    .out(multiplexer_7_out), .sel(SBSELC));

  // Other names for the same wires on the sheet: Reset = in_1
endmodule

module GRF (
  input  CLK,
  input  Reset,
  input  WE,
  input  [4:0] A1,
  input  [4:0] A2,
  input  [4:0] A3,
  input  [31:0] WD,
  output [31:0] RD1,
  output [31:0] RD2
);

  wire [31:0] data1, data2, data3, data4, data5, data6, data7, data8, data9, data10, data11, data12, data13,
       data14, data15, data16, data17, data18, data19, data20, data21, data22, data23, data24, data25,
       data26, data27, data28, data29, data30, data31, out0, out1, out2, out3, out4, out5, out6, out7, out8,
       out9, out10, out11, out12, out13, out14, out15, out16, out17, out18, out19, out20, out21, out22,
       out23, out24, out25, out26, out27, out28, out29, out30, out31;

  Demultiplexer #(.select(5), .width(32), .tristate("true")) demultiplexer_1 (
    .out1(data1), .out2(data2), .out3(data3), .out4(data4), .out5(data5), .out6(data6), .out7(data7),
    .out8(data8), .out9(data9), .out10(data10), .out11(data11), .out12(data12), .out13(data13),
    .out14(data14), .out15(data15), .out16(data16), .out17(data17), .out18(data18), .out19(data19),
    .out20(data20), .out21(data21), .out22(data22), .out23(data23), .out24(data24), .out25(data25),
    .out26(data26), .out27(data27), .out28(data28), .out29(data29), .out30(data30), .out31(data31), .in(WD),
    .sel(A3), .en(WE));  // open: out0
  Register #(.width(32)) _0 (.Q(out0), .clr(1'b1));  // open: D, en, clk
  Register #(.width(32)) _8 (.D(data8), .Q(out8), .clk(CLK), .clr(Reset));  // open: en
  Register #(.width(32)) _16 (.D(data16), .Q(out16), .clk(CLK), .clr(Reset));  // open: en
  Register #(.width(32)) _24 (.D(data24), .Q(out24), .clk(CLK), .clr(Reset));  // open: en
  Register #(.width(32)) _1 (.D(data1), .Q(out1), .clk(CLK), .clr(Reset));  // open: en
  Register #(.width(32)) _9 (.D(data9), .Q(out9), .clk(CLK), .clr(Reset));  // open: en
  Register #(.width(32)) _17 (.D(data17), .Q(out17), .clk(CLK), .clr(Reset));  // open: en
  Register #(.width(32)) _25 (.D(data25), .Q(out25), .clk(CLK), .clr(Reset));  // open: en
  Register #(.width(32)) _2 (.D(data2), .Q(out2), .clk(CLK), .clr(Reset));  // open: en
  Register #(.width(32)) _10 (.D(data10), .Q(out10), .clk(CLK), .clr(Reset));  // open: en
  Register #(.width(32)) _18 (.D(data18), .Q(out18), .clk(CLK), .clr(Reset));  // open: en
  Register #(.width(32)) _26 (.D(data26), .Q(out26), .clk(CLK), .clr(Reset));  // open: en
  Register #(.width(32)) _3 (.D(data3), .Q(out3), .clk(CLK), .clr(Reset));  // open: en
  Register #(.width(32)) _11 (.D(data11), .Q(out11), .clk(CLK), .clr(Reset));  // open: en
  Register #(.width(32)) _19 (.D(data19), .Q(out19), .clk(CLK), .clr(Reset));  // open: en
  Register #(.width(32)) _27 (.D(data27), .Q(out27), .clk(CLK), .clr(Reset));  // open: en
  Register #(.width(32)) _4 (.D(data4), .Q(out4), .clk(CLK), .clr(Reset));  // open: en
  Register #(.width(32)) _12 (.D(data12), .Q(out12), .clk(CLK), .clr(Reset));  // open: en
  Register #(.width(32)) _20 (.D(data20), .Q(out20), .clk(CLK), .clr(Reset));  // open: en
  Register #(.width(32)) _28 (.D(data28), .Q(out28), .clk(CLK), .clr(Reset));  // open: en
  Register #(.width(32)) _5 (.D(data5), .Q(out5), .clk(CLK), .clr(Reset));  // open: en
  Register #(.width(32)) _21 (.D(data21), .Q(out21), .clk(CLK), .clr(Reset));  // open: en
  Register #(.width(32)) _29 (.D(data29), .Q(out29), .clk(CLK), .clr(Reset));  // open: en
  Register #(.width(32)) _13 (.D(data13), .Q(out13), .clk(CLK), .clr(Reset));  // open: en
  Register #(.width(32)) _6 (.D(data6), .Q(out6), .clk(CLK), .clr(Reset));  // open: en
  Register #(.width(32)) _14 (.D(data14), .Q(out14), .clk(CLK), .clr(Reset));  // open: en
  Register #(.width(32)) _22 (.D(data22), .Q(out22), .clk(CLK), .clr(Reset));  // open: en
  Register #(.width(32)) _30 (.D(data30), .Q(out30), .clk(CLK), .clr(Reset));  // open: en
  Register #(.width(32)) _31 (.D(data31), .Q(out31), .clk(CLK), .clr(Reset));  // open: en
  Register #(.width(32)) _7 (.D(data7), .Q(out7), .clk(CLK), .clr(Reset));  // open: en
  Register #(.width(32)) _15 (.D(data15), .Q(out15), .clk(CLK), .clr(Reset));  // open: en
  Register #(.width(32)) _23 (.D(data23), .Q(out23), .clk(CLK), .clr(Reset));  // open: en
  Multiplexer #(.select(5), .width(32), .disabled(0), .enable("false")) multiplexer_1 (
    .in0(out0), .in1(out1), .in2(out2), .in3(out3), .in4(out4), .in5(out5), .in6(out6), .in7(out7),
    .in8(out8), .in9(out9), .in10(out10), .in11(out11), .in12(out12), .in13(out13), .in14(out14),
    .in15(out15), .in16(out16), .in17(out17), .in18(out18), .in19(out19), .in20(out20), .in21(out21),
    .in22(out22), .in23(out23), .in24(out24), .in25(out25), .in26(out26), .in27(out27), .in28(out28),
    .in29(out29), .in30(out30), .in31(out31), .out(RD1), .sel(A1));
  Multiplexer #(.select(5), .width(32), .disabled(0), .enable("false")) multiplexer_2 (
    .in0(out0), .in1(out1), .in2(out2), .in3(out3), .in4(out4), .in5(out5), .in6(out6), .in7(out7),
    .in8(out8), .in9(out9), .in10(out10), .in11(out11), .in12(out12), .in13(out13), .in14(out14),
    .in15(out15), .in16(out16), .in17(out17), .in18(out18), .in19(out19), .in20(out20), .in21(out21),
    .in22(out22), .in23(out23), .in24(out24), .in25(out25), .in26(out26), .in27(out27), .in28(out28),
    .in29(out29), .in30(out30), .in31(out31), .out(RD2), .sel(A2));
endmodule

module \分线器  (
  input  [31:0] in_1,
  output [5:0] OPcode,
  output [4:0] rs,
  output [4:0] rt,
  output [4:0] rd,
  output [4:0] shamt,
  output [5:0] func,
  output [15:0] imm0_16,
  output [25:0] imm26
);


  assign func = in_1[5:0];
  assign imm0_16 = in_1[15:0];
  assign imm26 = in_1[25:0];
  assign OPcode = in_1[31:26];
  assign rd = in_1[15:11];
  assign rs = in_1[25:21];
  assign rt = in_1[20:16];
  assign shamt = in_1[10:6];
endmodule

module NPC (
  input  [2:0] NPCOP,
  input  [4:0] Zero,
  input  [31:0] PC,
  input  [25:0] IMM26,
  input  [15:0] IMM16,
  input  [31:0] imm32,
  output [31:0] PC_4,
  output [31:0] NPC
);

  wire [31:0] adder_2_out, bit_extender_1_out, multiplexer_1_out, multiplexer_2_out, shifter_1_out;

  Adder #(.width(32)) adder_1 (.a(32'h4), .b(PC), .out(PC_4));  // open: cin, cout
  assign bit_extender_1_out = {{16{IMM16[15]}}, IMM16};  // Bit_Extender bit_extender_1
  Shifter #(.width(32)) shifter_1 (.in(bit_extender_1_out), .\dist (5'b00010), .out(shifter_1_out));
  Adder #(.width(32)) adder_2 (.a(PC_4), .b(shifter_1_out), .out(adder_2_out));  // open: cin, cout
  Multiplexer #(.width(32), .enable("false")) multiplexer_1 (
    .in0(PC_4), .in1(adder_2_out), .out(multiplexer_1_out), .sel(Zero[0]));
  Multiplexer #(.width(32), .enable("false")) multiplexer_2 (
    .in0(PC_4), .in1(adder_2_out), .out(multiplexer_2_out), .sel(Zero[1]));
  Multiplexer #(.select(3), .width(32), .enable("false")) multiplexer_3 (
    .in0(PC_4), .in1(multiplexer_1_out), .in2({PC[31:28], IMM26, 2'b00}), .in3(imm32),
    .in4(multiplexer_2_out), .out(NPC), .sel(NPCOP));  // open: in5, in6, in7

  // Other names for the same wires on the sheet: npc_t[2:0] = NPCOP; beq = Zero[0]; bgez = Zero[1]
endmodule

module ALU (
  input  [3:0] ALUOP,
  input  [31:0] A,
  input  [31:0] B,
  output [4:0] Zero,
  output [31:0] ALUOUT
);

  wire comparator_1_eq, comparator_1_gt;
  wire [31:0] adder_1_out, and_1_out, or_1_out, shifter_1_out, subtractor_1_out;

  Adder #(.width(32)) adder_1 (.a(A), .b(B), .out(adder_1_out));  // open: cin, cout
  Subtractor #(.width(32)) subtractor_1 (.a(A), .b(B), .out(subtractor_1_out));  // open: bin, bout
  assign or_1_out = A | B;  // OR_Gate or_1, 32 bits wide
  assign and_1_out = A & B;  // AND_Gate and_1, 32 bits wide
  Shifter #(.width(32)) shifter_1 (.in(B), .\dist (5'b10000), .out(shifter_1_out));
  Comparator #(.width(32)) comparator_1 (
    .a(A), .b({32{1'b0}}), .gt(comparator_1_gt), .eq(comparator_1_eq));  // open: lt
  or or_2 (Zero[1], comparator_1_gt, comparator_1_eq);
  Comparator #(.width(32)) comparator_2 (.a(subtractor_1_out), .b({32{1'b0}}), .eq(Zero[0]));  // open: gt, lt
  Multiplexer #(.select(4), .width(32), .enable("false")) multiplexer_1 (
    .in0(adder_1_out), .in1(subtractor_1_out), .in2(or_1_out), .in3(and_1_out), .in4(shifter_1_out),
    .out(ALUOUT), .sel(ALUOP));  // open: in5, in6, in7, in8, in9, in10, in11, in12, in13, in14, in15

  // Other names for the same wires on the sheet: beq = Zero[0]; BGEZ = Zero[1]
endmodule

module Control (
  input  [5:0] opcode,
  input  [5:0] func,
  output rfwe,
  output [2:0] RFA3MUX,
  output [1:0] DMDATAMUX,
  output [2:0] RFWDMUX,
  output [1:0] ALUAMUX,
  output [1:0] EXTOP,
  output DMWE,
  output [2:0] AUBMUX,
  output [3:0] ALUOP,
  output [2:0] npcop
);

  wire ADDIU, ADDU, BEQ, BGEZ, J, JAL, JR, LUI, LW, not_1_out, not_2_out, not_3_out, not_4_out, not_5_out,
       not_6_out, not_7_out, not_8_out, not_9_out, not_10_out, not_11_out, not_12_out, ORI, R, SB, SLL, SUBU,
       SW;

  not not_1 (not_1_out, opcode[5]);
  not not_2 (not_2_out, opcode[4]);
  or npcop2 (npcop[2], 1'b0, BGEZ);
  not not_3 (not_3_out, opcode[3]);
  or npcop1 (npcop[1], 1'b0, J, JAL, JR);
  not not_4 (not_4_out, opcode[2]);
  or npcop0 (npcop[0], 1'b0, BEQ, JR);
  or u_rfwe (rfwe, 1'b0, ORI, LW, LUI, ADDU, SUBU, SLL, JAL, ADDIU);
  not not_5 (not_5_out, opcode[1]);
  buf aluop3 (ALUOP[3], 1'b0);  // OR_Gate
  or aluop2 (ALUOP[2], 1'b0, LUI);
  not not_6 (not_6_out, opcode[0]);
  or aluop1 (ALUOP[1], 1'b0, ORI);
  or aluop0 (ALUOP[0], 1'b0, BEQ, SUBU);
  and u_R (R, ~opcode[5], ~opcode[4], ~opcode[3], ~opcode[2], ~opcode[1], ~opcode[0]);  // AND_Gate
  and u_ORI (ORI, not_1_out, not_2_out, opcode[3], opcode[2], not_5_out, opcode[0]);
  and u_LW (LW, opcode[5], not_2_out, not_3_out, not_4_out, opcode[1], opcode[0]);
  and u_SW (SW, opcode[5], not_2_out, opcode[3], not_4_out, opcode[1], opcode[0]);
  and u_LUI (LUI, not_1_out, not_2_out, opcode[3], opcode[2], opcode[1], opcode[0]);
  and u_BEQ (BEQ, not_1_out, not_2_out, not_3_out, opcode[2], not_5_out, not_6_out);
  and u_J (J, not_1_out, not_2_out, not_3_out, not_4_out, opcode[1], not_6_out);
  and u_JAL (JAL, not_1_out, not_2_out, not_3_out, not_4_out, opcode[1], opcode[0]);
  and u_ADDIU (ADDIU, not_1_out, not_2_out, opcode[3], not_4_out, not_5_out, opcode[0]);
  and u_SB (SB, opcode[5], not_2_out, opcode[3], not_4_out, not_5_out, not_6_out);
  and u_BGEZ (BGEZ, not_1_out, not_2_out, not_3_out, not_4_out, not_5_out, opcode[0]);
  or extop1 (EXTOP[1], 1'b0, SLL);
  or extop0 (EXTOP[0], 1'b0, ORI, LUI);
  or u_dmwe (DMWE, 1'b0, SW, SB);
  buf RFA3MUX2 (RFA3MUX[2], 1'b0);  // OR_Gate
  or RFA3MUX1 (RFA3MUX[1], 1'b0, JAL);
  not not_7 (not_7_out, func[5]);
  or RFA3MUX0 (RFA3MUX[0], 1'b0, ORI, LW, LUI, ADDIU);
  not not_8 (not_8_out, func[4]);
  buf RFWDMUX2 (RFWDMUX[2], 1'b0);  // OR_Gate
  not not_9 (not_9_out, func[3]);
  or RFWDMUX1 (RFWDMUX[1], 1'b0, JAL);
  or RFWDMUX0 (RFWDMUX[0], 1'b0, LW);
  not not_10 (not_10_out, func[2]);
  buf ALUBMUX2 (AUBMUX[2], 1'b0);  // OR_Gate
  not not_11 (not_11_out, func[1]);
  buf ALUBMUX1 (AUBMUX[1], 1'b0);  // OR_Gate
  or ALUBMUX0 (AUBMUX[0], 1'b0, ORI, LW, SW, LUI, SLL, ADDIU, SB);
  not not_12 (not_12_out, func[0]);
  buf ALUAMUX1 (ALUAMUX[1], 1'b0);  // OR_Gate
  or ALUAMUX0 (ALUAMUX[0], 1'b0, SLL);
  and u_ADDU (ADDU, func[5], not_8_out, not_9_out, R, not_10_out, not_11_out, func[0]);
  and u_SUBU (SUBU, func[5], not_8_out, not_9_out, not_10_out, func[1], func[0], R);
  and u_SLL (SLL, not_7_out, not_8_out, not_9_out, not_10_out, not_11_out, not_12_out, R);
  and u_JR (JR, not_7_out, not_8_out, func[3], not_10_out, not_11_out, not_12_out, R);
  buf DMDATAMUX0 (DMDATAMUX[1], 1'b0);  // OR_Gate
  or DMDATAMUX1 (DMDATAMUX[0], 1'b0, SB);

  // Other names for the same wires on the sheet: f0 = func[0]; f1 = func[1]; f2 = func[2]; f3 = func[3]; f4 = func[4];
  //   f5 = func[5]; op0 = opcode[0]; op1 = opcode[1]; op2 = opcode[2]; op3 = opcode[3]; op4 = opcode[4];
  //   op5 = opcode[5]
endmodule
